// Logisim project cache.circ as structural Verilog: 1 circuit, main circuit cache
module cache (
  input  [13:0] CPU_Address,
  input  [31:0] code,
  input  CLOCK,
  input  RESET
);

  wire set1, set2, set3, set4;

  Register #(.width(1)) register_1 ();  // open: D, en, clk, Q, clr
  Register #(.width(1)) register_2 ();  // open: D, en, clk, Q, clr
  Register #(.width(1)) register_3 ();  // open: D, en, clk, Q, clr
  Register #(.width(1)) register_4 ();  // open: D, en, clk, Q, clr
  Register #(.width(1)) register_5 ();  // open: D, en, clk, Q, clr
  Register #(.width(1)) register_6 ();  // open: D, en, clk, Q, clr
  Register #(.width(1)) register_7 ();  // open: D, en, clk, Q, clr
  Register #(.width(1)) register_8 ();  // open: D, en, clk, Q, clr
  Register #(.width(1)) register_9 ();  // open: D, en, clk, Q, clr
  Register #(.width(1)) register_10 ();  // open: D, en, clk, Q, clr
  Register #(.width(1)) register_11 ();  // open: D, en, clk, Q, clr
  Register #(.width(1)) register_12 ();  // open: D, en, clk, Q, clr
  Decoder #(.select(2)) decoder_1 (
    .out0(set1), .out1(set2), .out2(set3), .out3(set4), .sel(CPU_Address[11:10]), .en(1'b1));
  Register #(.width(10)) register_13 (.en(1'b1));  // open: D, clk, Q, clr
  Register #(.width(10)) register_14 (.en(1'b1));  // open: D, clk, Q, clr
  Register #(.width(10)) register_15 (.en(1'b1));  // open: D, clk, Q, clr
  Register #(.width(10)) register_16 (.en(1'b1));  // open: D, clk, Q, clr
  Register #(.width(10)) register_17 (.en(1'b1));  // open: D, clk, Q, clr
  Register #(.width(10)) register_18 (.en(1'b1));  // open: D, clk, Q, clr
  Register #(.width(10)) register_19 (.en(1'b1));  // open: D, clk, Q, clr
  Register #(.width(10)) register_20 (.en(1'b1));  // open: D, clk, Q, clr
  // AND_Gate and_1 has open pins: in0=CLOCK, in1=set1, out=open
  // AND_Gate and_2 has open pins: in0=CLOCK, in1=set2, out=open
  // AND_Gate and_3 has open pins: in0=CLOCK, in1=set3, out=open
  // AND_Gate and_4 has open pins: in0=CLOCK, in1=set4, out=open
  set u_set1 (.RESET(RESET));  // open: data_in, word_index, block_index, CLOCK
  set u_set2 (.RESET(RESET));  // open: data_in, word_index, block_index, CLOCK
  set u_set3 (.RESET(RESET));  // open: data_in, word_index, block_index, CLOCK
  set u_set4 (.RESET(RESET));  // open: data_in, word_index, block_index, CLOCK
  Register #(.width(1)) register_21 ();  // open: D, en, clk, Q, clr
  Register #(.width(1)) register_22 ();  // open: D, en, clk, Q, clr
  Register #(.width(1)) register_23 ();  // open: D, en, clk, Q, clr
  Register #(.width(1)) register_24 ();  // open: D, en, clk, Q, clr
  Register #(.width(1)) register_25 ();  // open: D, en, clk, Q, clr
  Register #(.width(1)) register_26 ();  // open: D, en, clk, Q, clr
  Register #(.width(1)) register_27 ();  // open: D, en, clk, Q, clr
  Register #(.width(1)) register_28 ();  // open: D, en, clk, Q, clr

  // Other names for the same wires on the sheet: tag[9:0] = CPU_Address[9:0]; set_index[1:0] = CPU_Address[11:10];
  //   word_index[1:0] = CPU_Address[13:12]

  // Notes on the sheet:
  //   tag: 10 bit, set: 2bit, word: 2bit
  //   if 0: block1 else: block 2
  //   LRU bit
  //   LRU bit
  //   LRU bit
  //   LRU bit
  //   valid bit
  //   valid bit
  //   valid bit
  //   valid bit
  //   works: dirty bit/ tag bits/ transfering beetwin m.m and c.m and cpu / LRU
  //   tag array
  //   tag array
  //   tag array
  //   tag array
  //   dirty bit
  //   dirty bit
  //   dirty bit
  //   dirty bit
endmodule
